// Logisim project ALU Input.circ as structural Verilog: 1 circuit, main circuit main
module main (
  input  [15:0] Constante,
  input  [31:0] RT,
  input  Sign_Extend,
  input  Type_I,
  output [31:0] B
);

  wire [31:0] bit_extender_1_out, bit_extender_2_out, multiplexer_1_out;

  assign bit_extender_1_out = {{16{Constante[15]}}, Constante};  // Bit_Extender bit_extender_1
  Multiplexer #(.width(32), .enable("false")) multiplexer_1 (
    .in0(bit_extender_1_out), .in1(bit_extender_2_out), .out(multiplexer_1_out), .sel(Sign_Extend));
  assign bit_extender_2_out = {{16{1'b0}}, Constante};  // Bit_Extender bit_extender_2
  Multiplexer #(.width(32), .enable("false")) multiplexer_2 (.in0(RT), .in1(multiplexer_1_out), .out(B), .sel(Type_I));

  // Other names for the same wires on the sheet: cte[15:0] = Constante; SE = Sign_Extend

  // Notes on the sheet:
  //   ALU Input
endmodule
