// Logisim project ALU-Input.circ as structural Verilog: 2 circuits, main circuit ALU-Input
module ALU_Input (
  input  [31:0] RT,
  input  Type_I,
  input  [15:0] Const,
  input  Const_Extender_Selector,
  output [31:0] B
);

  wire [31:0] Const_t;

  Const_Extender const_extender_1 (.Selector(Const_Extender_Selector), .offset(Const), .Const_Ext(Const_t));
  Multiplexer #(.width(32), .enable("false")) multiplexer_1 (.in0(RT), .in1(Const_t), .out(B), .sel(Type_I));

  // Notes on the sheet:
  //   ALU-Input
endmodule

module Const_Extender (
  input  Selector,
  input  [15:0] offset,
  output [31:0] Const_Ext
);

  wire and_1_out;

  and and_1 (and_1_out, ~Selector, offset[15]);  // AND_Gate
  assign Const_Ext = {{16{and_1_out}}, offset};  // Bit_Extender bit_extender_1

  // Other names for the same wires on the sheet: const[15:0] = offset; I15 = offset[15]; Output[31:0] = Const_Ext

  // Notes on the sheet:
  //   CONST EXTENDER
endmodule
