// Logisim project ALU-Selector.circ as structural Verilog: 2 circuits, main circuit ALU-Operation-Selector
module ALU_Operation_Selector (
  input  add,
  input  addi,
  input  slt,
  input  slti,
  input  sub,
  input  sltu,
  input  \nor ,
  input  sltiu,
  input  mult,
  input  mulu,
  input  div,
  input  \and ,
  input  divu,
  input  andi,
  input  \or ,
  input  ori,
  input  \xor ,
  input  xori,
  output [3:0] ALU_Op_Selector
);

  wire Add_t, And_t, Or_t, priority_encoder_1_gs, Slt_t, Sltu_t, Xor_t;
  wire [3:0] priority_encoder_1_out;

  or or_1 (Add_t, add, addi);
  or or_2 (Slt_t, slt, slti);
  or or_3 (Sltu_t, sltu, sltiu);
  or or_4 (And_t, \and , andi);
  or or_5 (Or_t, \or , ori);
  or or_6 (Xor_t, \xor , xori);
  Priority_Encoder #(.select(4), .disabled(0)) priority_encoder_1 (
    .in0(Add_t), .in1(sub), .in2(Slt_t), .in3(Sltu_t), .in4(And_t), .in5(Or_t), .in6(\nor ), .in7(Xor_t),
    .in8(mult), .in9(mulu), .in10(div), .in11(divu), .out(priority_encoder_1_out),
    .gs(priority_encoder_1_gs), .en_in(1'b1));  // open: in12, in13, in14, in15, en_out
  Multiplexer #(.width(4), .enable("false")) multiplexer_1 (
    .in0(4'b0000), .in1(priority_encoder_1_out), .out(ALU_Op_Selector), .sel(priority_encoder_1_gs));

  // Notes on the sheet:
  //   ALU Operations
endmodule

module Const_Extender_Selector (
  input  andi,
  input  ori,
  input  xori,
  output Selector
);

  or or_1 (Selector, andi, ori, xori);
endmodule
