// Logisim project ALU.circ as structural Verilog: 8 circuits, main circuit Multiplication
module ALU (
  input  [31:0] Data_A,
  input  [31:0] Data_B,
  input  [3:0] Selector,
  output [31:0] ALU_Output,
  output [31:0] High,
  output Zero_Flag,
  output Negative_Flag
);

  wire slt_bit, sltu_bit;
  wire [1:0] MultDivSelector;
  wire [31:0] Add, And, DivHigh, DivLow, DivuHigh, DivuLow, MultDivLow, MultHigh, multiplexer_2_out, MultLow,
       MuluHigh, MuluLow, Nor, Or, slt, sltu, Sub, Xor;

  Adder #(.width(32)) adder_1 (.a(Data_A), .b(Data_B), .out(Add));  // open: cin, cout
  Multiplier #(.width(32)) multiplier_1 (.a(Data_A), .b(Data_B), .out(MuluLow), .cout(MuluHigh));  // open: cin
  Multiplication multiplication_1 (.A(Data_A), .B(Data_B), .Low(MultLow), .High(MultHigh));
  Comparator #(.width(32)) comparator_1 (.a(Data_A), .b(Data_B), .lt(slt_bit));  // open: gt, eq
  assign slt = {{31{1'b0}}, slt_bit};  // Bit_Extender bit_extender_1
  Multiplexer #(.select(2), .width(32), .enable("false")) multiplexer_1 (
    .in0(MultHigh), .in1(DivHigh), .in2(MuluHigh), .in3(DivuHigh), .out(High), .sel(MultDivSelector));
  or or_1 (MultDivSelector[0], Selector[1], Selector[2]);
  or or_2 (MultDivSelector[1], Selector[0], Selector[2]);
  Subtractor #(.width(32)) subtractor_1 (.a(Data_A), .b(Data_B), .out(Sub));  // open: bin, bout
  Divider #(.width(32)) divider_1 (.a(Data_A), .b(Data_B), .out(DivuLow), .rem(DivuHigh));  // open: upper
  Division division_1 (.A(Data_A), .B(Data_B), .Low(DivLow), .High(DivHigh));
  Comparator #(.width(32), .mode("unsigned")) comparator_2 (.a(Data_A), .b(Data_B), .lt(sltu_bit));  // open: gt, eq
  assign sltu = {{31{1'b0}}, sltu_bit};  // Bit_Extender bit_extender_2
  Multiplexer #(.select(3), .width(32), .enable("false")) multiplexer_2 (
    .in0(Add), .in1(Sub), .in2(slt), .in3(sltu), .in4(And), .in5(Or), .in6(Nor), .in7(Xor),
    .out(multiplexer_2_out), .sel(Selector[2:0]));
  Multiplexer #(.select(2), .width(32), .enable("false")) multiplexer_3 (
    .in0(MultLow), .in1(DivLow), .in2(MuluLow), .in3(DivuLow), .out(MultDivLow), .sel(MultDivSelector));
  Multiplexer #(.width(32), .enable("false")) multiplexer_4 (
    .in0(multiplexer_2_out), .in1(MultDivLow), .out(ALU_Output), .sel(Selector[3]));
  assign And = Data_A & Data_B;  // AND_Gate and_1, 32 bits wide
  assign Or = Data_A | Data_B;  // OR_Gate or_3, 32 bits wide
  Comparator #(.width(32)) comparator_3 (
    .a(ALU_Output), .b({32{1'b0}}), .eq(Zero_Flag), .lt(Negative_Flag));  // open: gt
  assign Nor = ~(Data_A | Data_B);  // NOR_Gate nor_1, 32 bits wide
  assign Xor = Data_A ^ Data_B;  // XOR_Gate xor_1, 32 bits wide

  // Other names for the same wires on the sheet: A[31:0] = Data_A; B[31:0] = Data_B; Output[31:0] = ALU_Output;
  //   Selector_t[2:0] = Selector[2:0]; IsMultDiv = Selector[3]

  // Notes on the sheet:
  //   INPUTS
  //   ARITHMETIC
  //   LOGIC
  //   OUTPUTS
endmodule

module Multiplication (
  input  [31:0] A,
  input  [31:0] B,
  output [31:0] Low,
  output [31:0] High
);

  wire NegOut, selectorA, selectorB;
  wire [31:0] multiplier_1_cout, multiplier_1_out, negative_1_output, negative_2_output,
       negative_to_positive_1_output, negative_to_positive_2_output;

  // Probe on A
  // Probe on B
  Negative_To_Positive negative_to_positive_1 (.A(A), .Output(negative_to_positive_1_output), .Negative(selectorA));
  Negative_To_Positive negative_to_positive_2 (.A(B), .Output(negative_to_positive_2_output), .Negative(selectorB));
  Multiplier #(.width(32)) multiplier_1 (
    .a(negative_to_positive_1_output), .b(negative_to_positive_2_output), .out(multiplier_1_out),
    .cout(multiplier_1_cout));  // open: cin
  xor xor_1 (NegOut, selectorA, selectorB);
  Multiplexer #(.width(32), .enable("false")) multiplexer_1 (
    .in0(multiplier_1_out), .in1(negative_1_output), .out(Low), .sel(NegOut));
  Negative negative_1 (.A(multiplier_1_out), .Output(negative_1_output));
  Multiplexer #(.width(32), .enable("false")) multiplexer_2 (
    .in0(multiplier_1_cout), .in1(negative_2_output), .out(High), .sel(NegOut));
  Negative negative_2 (.A(multiplier_1_cout), .Output(negative_2_output));
  // Probe on Low
  // Probe on High
endmodule

module Division (
  input  [31:0] A,
  input  [31:0] B,
  output [31:0] Low,
  output [31:0] High
);

  wire NegOut, selectorA, selectorB;
  wire [31:0] divider_1_out, divider_1_rem, negative_1_output, negative_2_output,
       negative_to_positive_1_output, negative_to_positive_2_output;

  // Probe on A
  // Probe on B
  Negative_To_Positive negative_to_positive_1 (.A(A), .Output(negative_to_positive_1_output), .Negative(selectorA));
  Negative_To_Positive negative_to_positive_2 (.A(B), .Output(negative_to_positive_2_output), .Negative(selectorB));
  Divider #(.width(32)) divider_1 (
    .a(negative_to_positive_1_output), .b(negative_to_positive_2_output), .out(divider_1_out),
    .rem(divider_1_rem));  // open: upper
  xor xor_1 (NegOut, selectorA, selectorB);
  Negative negative_1 (.A(divider_1_out), .Output(negative_1_output));
  Negative negative_2 (.A(divider_1_rem), .Output(negative_2_output));
  Multiplexer #(.width(32), .enable("false")) multiplexer_1 (
    .in0(divider_1_out), .in1(negative_1_output), .out(Low), .sel(NegOut));
  Multiplexer #(.width(32), .enable("false")) multiplexer_2 (
    .in0(divider_1_rem), .in1(negative_2_output), .out(High), .sel(NegOut));
  // Probe on Low
  // Probe on High
endmodule

module ConstExtender (
  input  [15:0] in_1,
  input  in_2,
  input  in_3,
  input  in_4,
  output [31:0] out_5
);

  wire and_1_out, Selector;

  or or_1 (Selector, in_2, in_3, in_4);
  and and_1 (and_1_out, ~Selector, in_1[15]);  // AND_Gate
  assign out_5 = {{16{and_1_out}}, in_1};  // Bit_Extender bit_extender_1

  // Other names for the same wires on the sheet: andi = in_2; const[15:0] = in_1; I15 = in_1[15]; ori = in_3;
  //   Output[31:0] = out_5; xori = in_4
endmodule

module ALU_Encoder (
  input  add,
  input  \and ,
  input  addi,
  input  andi,
  input  mult,
  input  sub,
  input  \or ,
  input  mulu,
  input  ori,
  input  slt,
  input  slti,
  input  div,
  input  \nor ,
  input  sltu,
  input  \xor ,
  input  divu,
  input  sltui,
  input  xori,
  output [3:0] ALU_Selector
);

  wire add_t, and_t, or_t, slt_t, sltu_t, xor_t;

  or or_1 (add_t, add, addi);
  or or_2 (slt_t, slt, slti);
  or or_3 (sltu_t, sltu, sltui);
  or or_4 (ALU_Selector[0], sub, sltu_t, xor_t, or_t, mulu);
  or or_5 (and_t, \and , andi);
  or or_6 (or_t, \or , ori);
  or or_7 (xor_t, \xor , xori);
  or or_8 (ALU_Selector[1], slt_t, sltu_t, \nor , xor_t, div);
  or or_9 (ALU_Selector[2], and_t, or_t, \nor , xor_t, divu);
  or or_10 (ALU_Selector[3], mult, mulu, div, divu);

  // Other names for the same wires on the sheet: _0 = ALU_Selector[0]; _1 = ALU_Selector[1]; _2 = ALU_Selector[2];
  //   _3 = ALU_Selector[3]; sltiu = sltui

  // Notes on the sheet:
  //   ALU Operations
  //   Encoding
  //   Crafting Selector
endmodule

module Negative_To_Positive (
  input  [31:0] A,
  output [31:0] Output,
  output Negative
);

  wire [31:0] negative_1_output;

  // Probe on A
  Negative negative_1 (.A(A), .Output(negative_1_output));
  Multiplexer #(.width(32), .enable("false")) multiplexer_1 (
    .in0(A), .in1(negative_1_output), .out(Output), .sel(A[31]));
  // Probe on Output

  assign Negative = A[31];
endmodule

module Negative (
  input  [31:0] A,
  output [31:0] Output
);

  wire [31:0] not_1_out;

  // Probe on A
  assign not_1_out = ~A;  // NOT_Gate not_1, 32 bits wide
  Adder #(.width(32)) adder_1 (.a(not_1_out), .b(32'h1), .out(Output));  // open: cin, cout
  // Probe on Output
endmodule

module Instruction_Decoder (
  input  [31:0] Instruction,
  output [4:0] Rs,
  output [25:0] jump,
  output [4:0] Rt,
  output add,
  output \nor ,
  output pop,
  output push,
  output halt,
  output rnd,
  output addi,
  output beq,
  output j,
  output [4:0] Rd,
  output [15:0] cte,
  output sub,
  output \xor ,
  output tty,
  output kbd,
  output andi,
  output bne,
  output mult,
  output slt,
  output ori,
  output blez,
  output mulu,
  output sltu,
  output xori,
  output bgtz,
  output div,
  output mfhi,
  output slti,
  output bltz,
  output Type_I,
  output divu,
  output mflo,
  output sltiu,
  output lw,
  output \and ,
  output nop,
  output sw,
  output \or ,
  output jr
);

  wire _00_0000, _11_1000, _11_1111, comparator_5_eq, comparator_6_eq, comparator_7_eq, comparator_8_eq,
       comparator_13_eq, comparator_14_eq, comparator_15_eq, comparator_16_eq, comparator_22_eq,
       comparator_23_eq, comparator_24_eq, comparator_25_eq, comparator_30_eq, comparator_31_eq,
       comparator_32_eq, comparator_33_eq, comparator_34_eq, comparator_35_eq, comparator_36_eq,
       comparator_37_eq, comparator_38_eq, comparator_39_eq;

  Comparator #(.width(6)) comparator_1 (.a(Instruction[31:26]), .b({6{1'b0}}), .eq(_00_0000));  // open: gt, lt
  Comparator #(.width(6)) comparator_2 (.a(Instruction[31:26]), .b(6'b001000), .eq(addi));  // open: gt, lt
  Comparator #(.width(6)) comparator_3 (.a(Instruction[31:26]), .b(6'b001010), .eq(slti));  // open: gt, lt
  Comparator #(.width(6)) comparator_4 (.a(Instruction[31:26]), .b(6'b000110), .eq(blez));  // open: gt, lt
  and and_1 (add, _00_0000, comparator_5_eq);
  Comparator #(.width(6)) comparator_5 (.a(Instruction[5:0]), .b(6'b100000), .eq(comparator_5_eq));  // open: gt, lt
  and and_2 (div, _00_0000, comparator_6_eq);
  Comparator #(.width(6)) comparator_6 (.a(Instruction[5:0]), .b(6'b011010), .eq(comparator_6_eq));  // open: gt, lt
  and and_3 (\nor , _00_0000, comparator_7_eq);
  Comparator #(.width(6)) comparator_7 (.a(Instruction[5:0]), .b(6'b100111), .eq(comparator_7_eq));  // open: gt, lt
  and and_4 (mfhi, _00_0000, comparator_8_eq);
  Comparator #(.width(6)) comparator_8 (.a(Instruction[5:0]), .b(6'b010000), .eq(comparator_8_eq));  // open: gt, lt
  Comparator #(.width(6)) comparator_9 (.a(Instruction[31:26]), .b(6'b111000), .eq(_11_1000));  // open: gt, lt
  Comparator #(.width(6)) comparator_10 (.a(Instruction[31:26]), .b(6'b001100), .eq(andi));  // open: gt, lt
  Comparator #(.width(6)) comparator_11 (.a(Instruction[31:26]), .b(6'b001011), .eq(sltiu));  // open: gt, lt
  Comparator #(.width(6)) comparator_12 (.a(Instruction[31:26]), .b(6'b000111), .eq(bgtz));  // open: gt, lt
  Comparator #(.width(6)) comparator_13 (.a(Instruction[5:0]), .b(6'b100010), .eq(comparator_13_eq));  // open: gt, lt
  Comparator #(.width(6)) comparator_14 (.a(Instruction[5:0]), .b(6'b011011), .eq(comparator_14_eq));  // open: gt, lt
  Comparator #(.width(6)) comparator_15 (.a(Instruction[5:0]), .b(6'b101000), .eq(comparator_15_eq));  // open: gt, lt
  Comparator #(.width(6)) comparator_16 (.a(Instruction[5:0]), .b(6'b010010), .eq(comparator_16_eq));  // open: gt, lt
  Comparator #(.width(6)) comparator_17 (.a(Instruction[31:26]), .b(6'b101011), .eq(sw));  // open: gt, lt
  and and_5 (sub, _00_0000, comparator_13_eq);
  and and_6 (divu, _00_0000, comparator_14_eq);
  and and_7 (\xor , _00_0000, comparator_15_eq);
  and and_8 (mflo, _00_0000, comparator_16_eq);
  Comparator #(.width(6)) comparator_18 (.a(Instruction[31:26]), .b({6{1'b1}}), .eq(_11_1111));  // open: gt, lt
  Comparator #(.width(6)) comparator_19 (.a(Instruction[31:26]), .b(6'b001101), .eq(ori));  // open: gt, lt
  Comparator #(.width(6)) comparator_20 (.a(Instruction[31:26]), .b(6'b000100), .eq(beq));  // open: gt, lt
  Comparator #(.width(6)) comparator_21 (.a(Instruction[31:26]), .b(6'b000001), .eq(bltz));  // open: gt, lt
  Comparator #(.width(6)) comparator_22 (.a(Instruction[5:0]), .b(6'b011000), .eq(comparator_22_eq));  // open: gt, lt
  Comparator #(.width(6)) comparator_23 (.a(Instruction[5:0]), .b(6'b100100), .eq(comparator_23_eq));  // open: gt, lt
  Comparator #(.width(6)) comparator_24 (.a(Instruction[5:0]), .b(6'b101010), .eq(comparator_24_eq));  // open: gt, lt
  Comparator #(.width(6)) comparator_25 (.a(Instruction[5:0]), .b({6{1'b0}}), .eq(comparator_25_eq));  // open: gt, lt
  and and_9 (mult, _00_0000, comparator_22_eq);
  and and_10 (\and , _00_0000, comparator_23_eq);
  and and_11 (slt, _00_0000, comparator_24_eq);
  and and_12 (nop, _00_0000, comparator_25_eq);
  Comparator #(.width(6)) comparator_26 (.a(Instruction[31:26]), .b(6'b000010), .eq(j));  // open: gt, lt
  Comparator #(.width(6)) comparator_27 (.a(Instruction[31:26]), .b(6'b001110), .eq(xori));  // open: gt, lt
  Comparator #(.width(6)) comparator_28 (.a(Instruction[31:26]), .b(6'b000101), .eq(bne));  // open: gt, lt
  Comparator #(.width(6)) comparator_29 (.a(Instruction[31:26]), .b(6'b100011), .eq(lw));  // open: gt, lt
  Comparator #(.width(6)) comparator_30 (.a(Instruction[5:0]), .b(6'b011001), .eq(comparator_30_eq));  // open: gt, lt
  Comparator #(.width(6)) comparator_31 (.a(Instruction[5:0]), .b(6'b100101), .eq(comparator_31_eq));  // open: gt, lt
  Comparator #(.width(6)) comparator_32 (.a(Instruction[5:0]), .b(6'b101011), .eq(comparator_32_eq));  // open: gt, lt
  Comparator #(.width(6)) comparator_33 (.a(Instruction[5:0]), .b(6'b001000), .eq(comparator_33_eq));  // open: gt, lt
  Comparator #(.width(6)) comparator_34 (.a(Instruction[5:0]), .b({6{1'b0}}), .eq(comparator_34_eq));  // open: gt, lt
  Comparator #(.width(6)) comparator_35 (.a(Instruction[5:0]), .b(6'b000001), .eq(comparator_35_eq));  // open: gt, lt
  and and_13 (mulu, _00_0000, comparator_30_eq);
  and and_14 (\or , _00_0000, comparator_31_eq);
  and and_15 (sltu, _00_0000, comparator_32_eq);
  and and_16 (jr, _00_0000, comparator_33_eq);
  and and_17 (pop, comparator_34_eq, _11_1000);
  and and_18 (push, _11_1000, comparator_35_eq);
  or or_1 (Type_I, addi, andi, ori, xori, slti, sltiu, beq, bne, blez, bgtz, bltz, lw, sw);
  Comparator #(.width(6)) comparator_36 (.a(Instruction[5:0]), .b({6{1'b1}}), .eq(comparator_36_eq));  // open: gt, lt
  Comparator #(.width(6)) comparator_37 (.a(Instruction[5:0]), .b(6'b000001), .eq(comparator_37_eq));  // open: gt, lt
  Comparator #(.width(6)) comparator_38 (.a(Instruction[5:0]), .b(6'b000010), .eq(comparator_38_eq));  // open: gt, lt
  Comparator #(.width(6)) comparator_39 (.a(Instruction[5:0]), .b(6'b000100), .eq(comparator_39_eq));  // open: gt, lt
  and and_19 (halt, _11_1111, comparator_36_eq);
  and and_20 (tty, _11_1111, comparator_37_eq);
  and and_21 (rnd, _11_1111, comparator_38_eq);
  and and_22 (kbd, _11_1111, comparator_39_eq);

  assign cte = Instruction[15:0];
  assign jump = Instruction[25:0];
  assign Rd = Instruction[15:11];
  assign Rs = Instruction[25:21];
  assign Rt = Instruction[20:16];

  // Other names for the same wires on the sheet: const[15:0] = Instruction[15:0]; func__code[5:0] = Instruction[5:0];
  //   op__code[5:0] = Instruction[31:26]

  // Notes on the sheet:
  //   op. code: 00 0000
  //   Type R 
  //   op. code: 11 1000
  //   op. code: 11 1111
  //   Type I
  //   --------
  //   Type J
  //   --------
endmodule
