// Logisim project Branch Control.circ as structural Verilog: 1 circuit, main circuit Branch-Control
module Branch_Control (
  input  [31:0] in_1,
  input  [31:0] in_2,
  input  [31:0] in_3,
  input  [25:0] in_4,
  input  [15:0] in_5,
  input  [6:0] Selector,
  output [31:0] PC_prime
);

  wire and_1_out, and_2_out, and_3_out, and_4_out, and_5_out, comparator_1_eq, or_2_out, RS_0, RS__0, RS__RT;
  wire [1:0] or_3_out;
  wire [13:0] bit_extender_1_out;
  wire [31:0] PC_4, PC_4_x;

  Comparator #(.width(32)) comparator_1 (.a(in_1), .b({32{1'b0}}), .eq(comparator_1_eq), .lt(RS_0));  // open: gt
  Comparator #(.width(32)) comparator_2 (.a(in_1), .b(in_2), .eq(RS__RT));  // open: gt, lt
  Adder #(.width(32)) adder_1 (.a(in_3), .b(32'h4), .out(PC_4));  // open: cin, cout
  assign bit_extender_1_out = {{13{in_5[15]}}, in_5[15]};  // Bit_Extender bit_extender_1
  or or_1 (RS__0, comparator_1_eq, RS_0);
  Adder #(.width(32)) adder_2 (.a(PC_4), .b({bit_extender_1_out, in_5, 2'b00}), .out(PC_4_x));  // open: cin, cout
  and and_1 (and_1_out, Selector[0], RS__RT);
  and and_2 (and_2_out, ~RS__RT, Selector[1]);  // AND_Gate
  and and_3 (and_3_out, Selector[2], RS__0);
  and and_4 (and_4_out, ~RS__0, Selector[3]);  // AND_Gate
  and and_5 (and_5_out, RS_0, Selector[4]);
  or or_2 (or_2_out, and_1_out, and_2_out, and_3_out, and_4_out, and_5_out);
  or or_3 (or_3_out[0], or_2_out, Selector[5]);
  or or_4 (or_3_out[1], Selector[5], Selector[6]);
  Multiplexer #(.select(2), .width(32), .enable("false")) multiplexer_1 (
    .in0(PC_4), .in1(PC_4_x), .in2({in_3[31:28], in_4, 2'b00}), .in3(in_1), .out(PC_prime), .sel(or_3_out));

  // Other names for the same wires on the sheet: offset[15:0] = in_5; dest[25:0] = in_4;
  //   jmp[31:2] = {in_3[31:28], in_4}; PC[31:0] = in_3; RS[31:0] = in_1; RT[31:0] = in_2; beq = Selector[0];
  //   bne = Selector[1]; blez = Selector[2]; bgtz = Selector[3]; bltz = Selector[4]; jr = Selector[5];
  //   j = Selector[6]

  // Notes on the sheet:
  //   Branch Control
endmodule
