// Logisim project Branch-Control-Selector.circ as structural Verilog: 2 circuits, main circuit Branch-Control-Pre-Input-Selector
module Branch_Control_Pre_Input_Selector (
  input  beq,
  input  bne,
  input  blez,
  input  bgtz,
  input  bltz,
  output [1:0] Pre_Selector
);

  or or_1 (Pre_Selector[0], beq, bne);
  or or_2 (Pre_Selector[1], blez, bgtz, bltz);
endmodule

module Branch_Control_Selector_borrar (
  input  beq,
  input  bne,
  input  blez,
  input  bgtz,
  input  bltz,
  input  jr,
  input  j,
  input  Zero_Flag,
  input  Neg_Flag,
  output [1:0] Selector
);

  wire and_1_out, and_2_out, and_3_out, and_4_out, and_5_out, and_6_out, and_7_out, and_8_out, or_1_out;

  and and_1 (and_1_out, Zero_Flag, ~Neg_Flag);  // AND_Gate
  or or_1 (or_1_out, Zero_Flag, Neg_Flag);
  and and_2 (and_2_out, ~Zero_Flag, ~Neg_Flag);  // AND_Gate
  and and_3 (and_3_out, ~Zero_Flag, Neg_Flag);  // AND_Gate
  and and_4 (and_4_out, beq, and_1_out);
  and and_5 (and_5_out, bne, ~Zero_Flag);  // AND_Gate
  and and_6 (and_6_out, blez, or_1_out);
  and and_7 (and_7_out, bgtz, and_2_out);
  and and_8 (and_8_out, bltz, and_3_out);
  or or_2 (Selector[0], and_4_out, and_5_out, and_6_out, and_7_out, and_8_out, jr);
  or or_3 (Selector[1], jr, j);

  // Other names for the same wires on the sheet: Negative = Neg_Flag; Zero = Zero_Flag
endmodule
