// Logisim project Control Unit.circ as structural Verilog: 1 circuit, main circuit main
module main (
  input  clock,
  input  reset,
  input  is_kbd,
  input  is_tty,
  input  is_ALU,
  input  is_save,
  input  is_jump,
  input  is_read,
  input  is_write,
  input  use_HI_LO,
  input  ready_read,
  input  ready_write,
  input  halt,
  output get_data,
  output write_data,
  output PC_enable,
  output RF_enable,
  output Inst__Memory_enable,
  output tty_enable,
  output kbd_enable,
  output \end ,
  output HI_LO_en
);

  wire demultiplexer_1_out0, demultiplexer_1_out1, demultiplexer_3_out0, demultiplexer_3_out1,
       demultiplexer_4_out0, demultiplexer_5_out3, END_q, Fetch_instruction_q, get_data_1, get_data_2,
       Idle_q, kbd_clear, MEM, mem_t, multiplexer_1_out, next_inst, not_1_out, or_4_out, or_5_out, or_8_out,
       SAVE, Save_inst_q, save_t, upd_PC, update_PC, wait_for_RAM_q;
  wire [1:0] exe_select;

  or or_1 (SAVE, is_ALU, is_save);
  or or_2 (MEM, is_write, is_read);
  or or_3 (update_PC, is_jump, is_tty);
  or or_4 (or_4_out, demultiplexer_1_out0, reset);
  Demultiplexer #(.enable("false")) demultiplexer_1 (
    .out0(demultiplexer_1_out0), .out1(demultiplexer_1_out1), .in(Idle_q), .sel(not_1_out));
  D_Flip_Flop Idle (.clk(clock), .D(or_4_out), .Q(Idle_q));  // open: Qn, preset, en, reset
  or or_5 (or_5_out, demultiplexer_3_out0, mem_t);
  Demultiplexer #(.enable("false")) demultiplexer_2 (.out0(get_data_2), .out1(write_data), .in(mem_t), .sel(is_write));
  or or_6 (get_data, get_data_1, get_data_2);
  and and_1 (kbd_enable, kbd_clear, is_kbd);
  not not_1 (not_1_out, reset);
  or or_7 (get_data_1, next_inst, demultiplexer_1_out1);
  D_Flip_Flop wait_for_RAM (.clk(clock), .D(or_5_out), .Q(wait_for_RAM_q), .reset(reset));  // open: Qn, preset, en
  or or_8 (or_8_out, demultiplexer_4_out0, get_data_1);
  Demultiplexer #(.enable("false")) demultiplexer_3 (
    .out0(demultiplexer_3_out0), .out1(demultiplexer_3_out1), .in(wait_for_RAM_q), .sel(multiplexer_1_out));
  Multiplexer #(.enable("false")) multiplexer_1 (
    .in0(ready_read), .in1(ready_write), .out(multiplexer_1_out), .sel(is_write));
  and and_2 (tty_enable, PC_enable, is_tty);
  and and_3 (HI_LO_en, RF_enable, use_HI_LO);
  Priority_Encoder #(.select(2)) priority_encoder_1 (
    .in0(SAVE), .in1(MEM), .in2(update_PC), .in3(halt), .out(exe_select), .en_in(1'b1));  // open: gs, en_out
  D_Flip_Flop Fetch_instruction (
    .clk(clock), .D(or_8_out), .Q(Fetch_instruction_q), .reset(reset));  // open: Qn, preset, en
  Demultiplexer #(.enable("false")) demultiplexer_4 (
    .out0(demultiplexer_4_out0), .out1(Inst__Memory_enable), .in(Fetch_instruction_q), .sel(ready_read));
  or or_9 (RF_enable, demultiplexer_3_out1, save_t);
  D_Flip_Flop u_Save (.clk(clock), .D(RF_enable), .Q(kbd_clear), .reset(reset));  // open: Qn, preset, en
  or or_10 (PC_enable, kbd_clear, upd_PC);
  D_Flip_Flop Save_inst (.clk(clock), .D(Inst__Memory_enable), .Q(Save_inst_q), .reset(reset));  // open: Qn, preset, en
  Demultiplexer #(.select(2), .enable("false")) demultiplexer_5 (
    .out0(save_t), .out1(mem_t), .out2(upd_PC), .out3(demultiplexer_5_out3), .in(Save_inst_q),
    .sel(exe_select));
  D_Flip_Flop u_Update_PC (.clk(clock), .D(PC_enable), .Q(next_inst), .reset(reset));  // open: Qn, preset, en
  or or_11 (\end , END_q, demultiplexer_5_out3);
  D_Flip_Flop u_END (.clk(clock), .D(\end ), .Q(END_q), .reset(reset));  // open: Qn, preset, en

  // Other names for the same wires on the sheet: clk = clock; IM_en = Inst__Memory_enable; ready_r = ready_read;
  //   ready_w = ready_write; HI_LO = RF_enable; RF_en = RF_enable; tty_en = tty_enable; PC_en = PC_enable;
  //   tty_out = PC_enable

  // Notes on the sheet:
  //   Outputs
  //   Inputs
endmodule
