// Logisim project HI-LO.circ as structural Verilog: 1 circuit, main circuit HI-LO
module HI_LO (
  input  Hi_Lo_enable,
  input  Clock,
  input  [31:0] High_in,
  input  [31:0] Low_in,
  output [31:0] Low_out,
  output [31:0] High_out
);

  Register #(.width(32)) Low (.D(Low_in), .en(Hi_Lo_enable), .Q(Low_out), .clk(Clock));  // open: clr
  Register #(.width(32)) High (.D(High_in), .en(Hi_Lo_enable), .Q(High_out), .clk(Clock));  // open: clr

  // Other names for the same wires on the sheet: clk = Clock; EN = Hi_Lo_enable

  // Notes on the sheet:
  //   HI-LO
endmodule
