// Logisim project Instruction-Decoder.circ as structural Verilog: 9 circuits, main circuit Instruction-Decoder
module Instruction_Decoder (
  input  [31:0] Instruction,
  input  Is_instruction,
  output [3:0] ALU_Op_Selector,
  output [4:0] Rs,
  output [1:0] BC_Selector,
  output [4:0] Rt,
  output [2:0] BC_Flag_Condition,
  output [15:0] \const ,
  output Const_Ext,
  output [1:0] MA_Input_Selector,
  output [25:0] dest,
  output [2:0] RF_Input_Selector,
  output Is_Read,
  output use_HI_LO,
  output Is_Write,
  output sw,
  output Is_Jump,
  output is_kbd,
  output Is_RF,
  output push,
  output pop,
  output halt,
  output tty,
  output Type_I,
  output [4:0] Data_Adress
);

  wire _00_0000, _11_1000, _11_1111, add, addi, \and , andi, beq, bgtz, blez, bltz, bne, comparator_5_eq,
       comparator_6_eq, comparator_7_eq, comparator_8_eq, comparator_13_eq, comparator_14_eq,
       comparator_15_eq, comparator_16_eq, comparator_21_eq, comparator_22_eq, comparator_23_eq,
       comparator_24_eq, comparator_29_eq, comparator_30_eq, comparator_31_eq, comparator_32_eq,
       comparator_33_eq, comparator_34_eq, comparator_36_eq, comparator_37_eq, comparator_38_eq,
       comparator_39_eq, div, divu, j, jr, lw, mfhi, mflo, mult, mulu, nop, \nor , nor_1_out, \or , ori, rnd,
       slt, slti, sltiu, sltu, sub, \xor , xori;

  Comparator #(.width(6)) comparator_1 (.a(Instruction[31:26]), .b({6{1'b0}}), .eq(_00_0000));  // open: gt, lt
  Comparator #(.width(6)) comparator_2 (.a(Instruction[31:26]), .b(6'b001000), .eq(addi));  // open: gt, lt
  Comparator #(.width(6)) comparator_3 (.a(Instruction[31:26]), .b(6'b001010), .eq(slti));  // open: gt, lt
  Comparator #(.width(6)) comparator_4 (.a(Instruction[31:26]), .b(6'b000110), .eq(blez));  // open: gt, lt
  Comparator #(.width(6)) comparator_5 (.a(Instruction[5:0]), .b(6'b100000), .eq(comparator_5_eq));  // open: gt, lt
  Comparator #(.width(6)) comparator_6 (.a(Instruction[5:0]), .b(6'b011010), .eq(comparator_6_eq));  // open: gt, lt
  Comparator #(.width(6)) comparator_7 (.a(Instruction[5:0]), .b(6'b100111), .eq(comparator_7_eq));  // open: gt, lt
  Comparator #(.width(6)) comparator_8 (.a(Instruction[5:0]), .b(6'b010000), .eq(comparator_8_eq));  // open: gt, lt
  Branch_Control_Selector branch_control_selector_1 (
    .beq(beq), .bne(bne), .blez(blez), .bgtz(bgtz), .bltz(bltz), .jr(jr), .j(j), .BC_Selector(BC_Selector),
    .Flag_Condition(BC_Flag_Condition));
  Const_Extender_Selector const_extender_selector_1 (.andi(andi), .ori(ori), .xori(xori), .Selector(Const_Ext));
  and and_1 (add, _00_0000, comparator_5_eq);
  and and_2 (div, _00_0000, comparator_6_eq);
  and and_3 (\nor , _00_0000, comparator_7_eq);
  and and_4 (mfhi, _00_0000, comparator_8_eq);
  Comparator #(.width(6)) comparator_9 (.a(Instruction[31:26]), .b(6'b111000), .eq(_11_1000));  // open: gt, lt
  Comparator #(.width(6)) comparator_10 (.a(Instruction[31:26]), .b(6'b001100), .eq(andi));  // open: gt, lt
  Comparator #(.width(6)) comparator_11 (.a(Instruction[31:26]), .b(6'b001011), .eq(sltiu));  // open: gt, lt
  Comparator #(.width(6)) comparator_12 (.a(Instruction[31:26]), .b(6'b000111), .eq(bgtz));  // open: gt, lt
  Comparator #(.width(6)) comparator_13 (.a(Instruction[5:0]), .b(6'b100010), .eq(comparator_13_eq));  // open: gt, lt
  Comparator #(.width(6)) comparator_14 (.a(Instruction[5:0]), .b(6'b011011), .eq(comparator_14_eq));  // open: gt, lt
  Comparator #(.width(6)) comparator_15 (.a(Instruction[5:0]), .b(6'b101000), .eq(comparator_15_eq));  // open: gt, lt
  Comparator #(.width(6)) comparator_16 (.a(Instruction[5:0]), .b(6'b010010), .eq(comparator_16_eq));  // open: gt, lt
  and and_5 (sub, _00_0000, comparator_13_eq);
  and and_6 (divu, _00_0000, comparator_14_eq);
  and and_7 (\xor , _00_0000, comparator_15_eq);
  and and_8 (mflo, _00_0000, comparator_16_eq);
  MA_Input_Selector ma_input_selector_1 (
    .pop(pop), .push(push), .sw(sw), .lw(lw), .MA_selector(MA_Input_Selector), .is_inst(Is_instruction));
  RF_Input_Selector rf_input_selector_1 (
    .pop(pop), .lw(lw), .kbd(is_kbd), .rnd(rnd), .mfhi(mfhi), .mflo(mflo), .RF_Input_Sel(RF_Input_Selector));
  Comparator #(.width(6)) comparator_17 (.a(Instruction[31:26]), .b({6{1'b1}}), .eq(_11_1111));  // open: gt, lt
  Comparator #(.width(6)) comparator_18 (.a(Instruction[31:26]), .b(6'b001101), .eq(ori));  // open: gt, lt
  Comparator #(.width(6)) comparator_19 (.a(Instruction[31:26]), .b(6'b000100), .eq(beq));  // open: gt, lt
  Comparator #(.width(6)) comparator_20 (.a(Instruction[31:26]), .b(6'b000001), .eq(bltz));  // open: gt, lt
  Comparator #(.width(6)) comparator_21 (.a(Instruction[5:0]), .b(6'b011000), .eq(comparator_21_eq));  // open: gt, lt
  Comparator #(.width(6)) comparator_22 (.a(Instruction[5:0]), .b(6'b100100), .eq(comparator_22_eq));  // open: gt, lt
  Comparator #(.width(6)) comparator_23 (.a(Instruction[5:0]), .b(6'b101010), .eq(comparator_23_eq));  // open: gt, lt
  Comparator #(.width(6)) comparator_24 (.a(Instruction[5:0]), .b({6{1'b0}}), .eq(comparator_24_eq));  // open: gt, lt
  and and_9 (mult, _00_0000, comparator_21_eq);
  and and_10 (\and , _00_0000, comparator_22_eq);
  and and_11 (slt, _00_0000, comparator_23_eq);
  and and_12 (nop, _00_0000, comparator_24_eq);
  Comparator #(.width(6)) comparator_25 (.a(Instruction[31:26]), .b(6'b000010), .eq(j));  // open: gt, lt
  Comparator #(.width(6)) comparator_26 (.a(Instruction[31:26]), .b(6'b001110), .eq(xori));  // open: gt, lt
  Comparator #(.width(6)) comparator_27 (.a(Instruction[31:26]), .b(6'b000101), .eq(bne));  // open: gt, lt
  Comparator #(.width(6)) comparator_28 (.a(Instruction[31:26]), .b(6'b100011), .eq(lw));  // open: gt, lt
  ALU_Operation_Selector alu_operation_selector_1 (
    .add(add), .slt(slt), .sltu(sltu), .\nor (\nor ), .mult(mult), .mulu(mulu), .div(div), .divu(divu),
    .ALU_Op_Selector(ALU_Op_Selector), .addi(addi), .\and (\and ), .andi(andi), .\or (\or ), .ori(ori),
    .sltiu(sltiu), .slti(slti), .sub(sub), .\xor (\xor ), .xori(xori));
  Comparator #(.width(6)) comparator_29 (.a(Instruction[5:0]), .b(6'b011001), .eq(comparator_29_eq));  // open: gt, lt
  Comparator #(.width(6)) comparator_30 (.a(Instruction[5:0]), .b(6'b100101), .eq(comparator_30_eq));  // open: gt, lt
  Comparator #(.width(6)) comparator_31 (.a(Instruction[5:0]), .b(6'b101011), .eq(comparator_31_eq));  // open: gt, lt
  Comparator #(.width(6)) comparator_32 (.a(Instruction[5:0]), .b(6'b001000), .eq(comparator_32_eq));  // open: gt, lt
  Comparator #(.width(6)) comparator_33 (.a(Instruction[5:0]), .b({6{1'b0}}), .eq(comparator_33_eq));  // open: gt, lt
  Comparator #(.width(6)) comparator_34 (.a(Instruction[5:0]), .b(6'b000001), .eq(comparator_34_eq));  // open: gt, lt
  Comparator #(.width(6)) comparator_35 (.a(Instruction[31:26]), .b(6'b101011), .eq(sw));  // open: gt, lt
  and and_13 (mulu, _00_0000, comparator_29_eq);
  and and_14 (\or , _00_0000, comparator_30_eq);
  and and_15 (sltu, _00_0000, comparator_31_eq);
  and and_16 (jr, _00_0000, comparator_32_eq);
  and and_17 (pop, comparator_33_eq, _11_1000);
  and and_18 (push, _11_1000, comparator_34_eq);
  Is_HI_LO is_hi_lo_1 (.mult(mult), .mulu(mulu), .div(div), .divu(divu), .Is_Hi_Lo(use_HI_LO));
  Comparator #(.width(6)) comparator_36 (.a(Instruction[5:0]), .b({6{1'b1}}), .eq(comparator_36_eq));  // open: gt, lt
  Comparator #(.width(6)) comparator_37 (.a(Instruction[5:0]), .b(6'b000001), .eq(comparator_37_eq));  // open: gt, lt
  Comparator #(.width(6)) comparator_38 (.a(Instruction[5:0]), .b(6'b000010), .eq(comparator_38_eq));  // open: gt, lt
  Comparator #(.width(6)) comparator_39 (.a(Instruction[5:0]), .b(6'b000100), .eq(comparator_39_eq));  // open: gt, lt
  and and_19 (halt, _11_1111, comparator_36_eq);
  and and_20 (tty, _11_1111, comparator_37_eq);
  and and_21 (rnd, _11_1111, comparator_38_eq);
  and and_22 (is_kbd, _11_1111, comparator_39_eq);
  Is_Read is_read_1 (.pop(pop), .lw(lw), .Is_Read(Is_Read));
  Is_Write is_write_1 (.push(push), .sw(sw), .Is_Write(Is_Write));
  Is_Jump is_jump_1 (.BC_Selector(BC_Selector), .Is_Jump(Is_Jump));
  Is_RF is_rf_1 (
    .kbd(is_kbd), .rnd(rnd), .mfhi(mfhi), .mflo(mflo), .Is_RF(Is_RF), .Is_HI_LO(use_HI_LO), .halt(halt),
    .tty(tty), .nrwj(nor_1_out), .nop(nop));
  nor nor_1 (nor_1_out, Is_Read, Is_Write, Is_Jump);
  Multiplexer #(.width(5), .enable("false")) multiplexer_1 (
    .in0(Instruction[15:11]), .in1(Instruction[20:16]), .out(Data_Adress), .sel(Type_I));
  Type_I type_i_1 (
    .addi(addi), .slti(slti), .sltiu(sltiu), .Const_Ext(Const_Ext), .lw(lw), .sw(sw), .jr(jr),
    .BC_Selector(BC_Selector), .Type_I(Type_I));

  assign \const  = Instruction[15:0];
  assign dest = Instruction[25:0];
  assign Rs = Instruction[25:21];
  assign Rt = Instruction[20:16];

  // Other names for the same wires on the sheet: func__code[5:0] = Instruction[5:0]; Rd[4:0] = Instruction[15:11];
  //   op__code[5:0] = Instruction[31:26]; Is_inst = Is_instruction; kbd = is_kbd

  // Notes on the sheet:
  //   INPUT
  //   SELECTORS
  //   INSTRUCTION DECODER
  //   CU FLAGS
  //   OUTPUT
  //   DATA ADRESS
  //   TYPE I
endmodule

module RF_Input_Selector (
  input  pop,
  input  lw,
  input  kbd,
  input  rnd,
  input  mfhi,
  input  mflo,
  output [2:0] RF_Input_Sel
);

  wire priority_encoder_1_gs, ram;
  wire [2:0] priority_encoder_1_out;

  or or_1 (ram, pop, lw);
  Priority_Encoder #(.disabled(0)) priority_encoder_1 (
    .in1(kbd), .in2(rnd), .in3(ram), .in4(mfhi), .in5(mflo), .out(priority_encoder_1_out), .en_in(1'b1),
    .gs(priority_encoder_1_gs));  // open: in0, in6, in7, en_out
  Multiplexer #(.width(3), .enable("false")) multiplexer_1 (
    .in0(3'b000), .in1(priority_encoder_1_out), .out(RF_Input_Sel), .sel(priority_encoder_1_gs));

  // Notes on the sheet:
  //   RF Input Selector
endmodule

module MA_Input_Selector (
  input  pop,
  input  push,
  input  is_inst,
  input  sw,
  input  lw,
  output [1:0] MA_selector
);

  or or_1 (MA_selector[1], pop, is_inst, push);
  or or_2 (MA_selector[0], sw, is_inst, lw);

  // Notes on the sheet:
  //   MEMORY ADRESS
  //   Input Selector
endmodule

module Is_Read (
  input  pop,
  input  lw,
  output Is_Read
);

  or or_1 (Is_Read, pop, lw);

  // Notes on the sheet:
  //   Is Read
endmodule

module Is_Write (
  input  push,
  input  sw,
  output Is_Write
);

  or or_1 (Is_Write, push, sw);

  // Notes on the sheet:
  //   Is Write
endmodule

module Is_Jump (
  input  [1:0] BC_Selector,
  output Is_Jump
);

  or or_1 (Is_Jump, BC_Selector[0], BC_Selector[1]);

  // Notes on the sheet:
  //   Is Jump
endmodule

module Is_RF (
  input  nrwj,
  input  kbd,
  input  rnd,
  input  mfhi,
  input  mflo,
  input  Is_HI_LO,
  input  halt,
  input  tty,
  input  nop,
  output Is_RF
);

  wire nor_1_out, or_1_out;

  or or_1 (or_1_out, nrwj, kbd, rnd, mfhi, mflo);
  nor nor_1 (nor_1_out, Is_HI_LO, halt, tty, nop);
  and and_1 (Is_RF, or_1_out, nor_1_out);

  // Notes on the sheet:
  //   Is RF
endmodule

module Type_I (
  input  addi,
  input  slti,
  input  sltiu,
  input  Const_Ext,
  input  lw,
  input  sw,
  input  jr,
  input  [1:0] BC_Selector,
  output Type_I
);

  wire and_1_out, or_1_out;

  or or_1 (or_1_out, addi, slti, sltiu, Const_Ext, lw, sw);
  and and_1 (and_1_out, ~jr, BC_Selector[0]);  // AND_Gate
  or or_2 (Type_I, or_1_out, and_1_out);

  // Notes on the sheet:
  //   Type I
endmodule

module Is_HI_LO (
  input  mult,
  input  mulu,
  input  div,
  input  divu,
  output Is_Hi_Lo
);

  or or_1 (Is_Hi_Lo, mult, mulu, div, divu);

  // Notes on the sheet:
  //   IS HI-LO
endmodule
