// Logisim project Instruction-Memory.circ as structural Verilog: 1 circuit, main circuit Instruction-Memory
module Instruction_Memory (
  input  [31:0] Instruction,
  input  EN,
  input  Clock,
  input  Reset,
  output [31:0] Output
);

  Register #(.width(32)) register_1 (.D(Instruction), .en(EN), .Q(Output), .clk(Clock), .clr(Reset));

  // Notes on the sheet:
  //   Instruction Memory
endmodule
