// Logisim project Program Counter.circ as structural Verilog: 1 circuit, main circuit main
module main (
  input  in_1,
  input  in_2,
  input  in_3,
  input  [31:0] Input,
  output [31:0] Output
);

  Register #(.width(32)) register_1 (.D(Input), .en(in_2), .Q(Output), .clk(in_1), .clr(in_3));

  // Other names for the same wires on the sheet: clock = in_1; enable = in_2; reset = in_3

  // Notes on the sheet:
  //    COUNTER
  //   PROGRAM 
endmodule
