// Logisim project RAM Interaction.circ as structural Verilog: 5 circuits, main circuit RAM INTERACTOR
module RAM_INTERACTOR (
  input  [31:0] RAM_Output_0,
  input  [31:0] RAM_Output_1,
  input  [31:0] RAM_Output_2,
  input  [31:0] RAM_Output_3,
  input  [31:0] Dir_RAM,
  input  [31:0] data_in,
  input  [3:0] read_time,
  input  [3:0] write_time,
  input  clock,
  input  reset,
  input  write,
  input  get,
  output [31:0] RAM_Input_0,
  output [31:0] RAM_Input_1,
  output [31:0] RAM_Input_2,
  output [31:0] RAM_Input_3,
  output [31:0] data_out,
  output [15:0] Address,
  output [3:0] Mask,
  output CS,
  output R_W,
  output ready_data,
  output ready_write
);

  wire CSR;

  RAM_reader ram_reader_1 (
    .Bank0(RAM_Output_0), .Bank1(RAM_Output_1), .Bank2(RAM_Output_2), .Bank3(RAM_Output_3),
    .Dir_RAM(Dir_RAM), .RT(read_time), .clock(clock), .reset(reset), .get(get), .CSR(CSR),
    .ready_read(ready_data), .read_data(data_out));
  RAM_writer ram_writer_1 (
    .WT(write_time), .clock(clock), .Dir_RAM(Dir_RAM), .value(data_in), .write(write), .Bank0(RAM_Input_0),
    .Bank1(RAM_Input_1), .Bank2(RAM_Input_2), .Bank3(RAM_Input_3), .CSW(R_W), .ready_write(ready_write));
  Demultiplexer #(.select(2), .enable("false")) demultiplexer_1 (
    .out0(Mask[0]), .out1(Mask[1]), .out2(Mask[2]), .out3(Mask[3]), .in(1'b1), .sel(Dir_RAM[3:2]));
  or or_1 (CS, CSR, R_W);

  assign Address = Dir_RAM[19:4];

  // Other names for the same wires on the sheet: clk = clock; CSW = R_W; DR[31:0] = Dir_RAM; rd = ready_data;
  //   RI0[31:0] = RAM_Input_0; RI1[31:0] = RAM_Input_1; RI2[31:0] = RAM_Input_2; RI3[31:0] = RAM_Input_3;
  //   RO0[31:0] = RAM_Output_0; RO1[31:0] = RAM_Output_1; RO2[31:0] = RAM_Output_2; RO3[31:0] = RAM_Output_3;
  //   rst = reset; RT[3:0] = read_time; rw = ready_write; WT[3:0] = write_time

  // Notes on the sheet:
  //   RAM INTERACTOR
endmodule

module RAM_reader (
  input  [31:0] Bank0,
  input  [31:0] Bank1,
  input  [31:0] Bank2,
  input  [31:0] Bank3,
  input  [31:0] Dir_RAM,
  input  [3:0] RT,
  input  clock,
  input  reset,
  input  get,
  output CSR,
  output ready_read,
  output [31:0] read_data
);

  wire CS1, CS2, demultiplexer_1_out0, demultiplexer_1_out1, or_2_out;
  wire [31:0] bank3_t, inverse_bytes_1_out_2, multiplexer_1_out;

  or or_1 (CSR, CS1, CS2);
  or or_2 (or_2_out, demultiplexer_1_out0, get);
  Timer timer_1 (.in_1(CS1), .in_2(CS2), .in_3(clock), .Output(ready_read), .in_4(RT));
  D_Flip_Flop d_ff_1 (.clk(clock), .D(or_2_out), .Q(CS1));  // open: Qn, preset, en, reset
  Demultiplexer #(.enable("false")) demultiplexer_1 (
    .out0(demultiplexer_1_out0), .out1(demultiplexer_1_out1), .in(CS1), .sel(ready_read));
  D_Flip_Flop d_ff_2 (.clk(clock), .D(demultiplexer_1_out1), .Q(CS2));  // open: Qn, preset, en, reset
  Multiplexer #(.select(2), .width(32), .enable("false")) multiplexer_1 (
    .in0(Bank0), .in1(Bank1), .in2(Bank2), .in3(bank3_t), .out(multiplexer_1_out), .sel(Dir_RAM[3:2]));
  Inverse_Bytes inverse_bytes_1 (.in_1(multiplexer_1_out), .out_2(inverse_bytes_1_out_2));
  Register #(.width(32)) register_1 (.D(inverse_bytes_1_out_2), .Q(read_data), .clk(clock), .clr(reset));  // open: en

  // Other names for the same wires on the sheet: clk = clock; data[31:0] = read_data; Selector[1:0] = Dir_RAM[3:2];
  //   ready = ready_read; rst = reset; time_reset = CS2

  // Notes on the sheet:
  //   RAM READER
endmodule

module RAM_writer (
  input  [3:0] WT,
  input  clock,
  input  [31:0] Dir_RAM,
  input  [31:0] value,
  input  write,
  output [31:0] Bank0,
  output [31:0] Bank1,
  output [31:0] Bank2,
  output [31:0] Bank3,
  output CSW,
  output ready_write
);

  wire CS2, demultiplexer_1_out0, demultiplexer_1_out1, or_2_out, R_W;
  wire [31:0] inverse_bytes_1_out_2;

  or or_1 (CSW, R_W, CS2);
  or or_2 (or_2_out, demultiplexer_1_out0, write);
  D_Flip_Flop d_ff_1 (.clk(clock), .D(or_2_out), .Q(R_W));  // open: Qn, preset, en, reset
  Timer timer_1 (.in_1(R_W), .in_2(CS2), .in_3(clock), .Output(ready_write), .in_4(WT));
  Demultiplexer #(.enable("false")) demultiplexer_1 (
    .out0(demultiplexer_1_out0), .out1(demultiplexer_1_out1), .in(R_W), .sel(ready_write));
  D_Flip_Flop d_ff_2 (.clk(clock), .D(demultiplexer_1_out1), .Q(CS2));  // open: Qn, preset, en, reset
  Inverse_Bytes inverse_bytes_1 (.in_1(value), .out_2(inverse_bytes_1_out_2));
  Demultiplexer #(.select(2), .width(32), .enable("false")) demultiplexer_2 (
    .out0(Bank0), .out1(Bank1), .out2(Bank2), .out3(Bank3), .in(inverse_bytes_1_out_2), .sel(Dir_RAM[3:2]));

  // Other names for the same wires on the sheet: clk = clock; Selector[1:0] = Dir_RAM[3:2]; ready = ready_write;
  //   RT[3:0] = WT; time_reset = CS2

  // Notes on the sheet:
  //   RAM WRITER
endmodule

module Timer (
  input  in_1,
  input  in_2,
  input  in_3,
  input  [3:0] in_4,
  output Output
);

  wire [3:0] counter_1_q;

  Counter #(.width(4), .max('hf)) counter_1 (
    .count(in_1), .Q(counter_1_q), .clk(in_3), .clr(in_2));  // open: load, D, carry
  Comparator #(.width(4)) comparator_1 (.a(in_4), .b(counter_1_q), .eq(Output));  // open: gt, lt

  // Other names for the same wires on the sheet: clock = in_3; ready = Output; reset = in_2; start = in_1;
  //   wait_time[3:0] = in_4

  // Notes on the sheet:
  //   TIMER
endmodule

module Inverse_Bytes (
  input  [31:0] in_1,
  output [31:0] out_2
);


  assign out_2 = {in_1[7:0], in_1[15:8], in_1[23:16], in_1[31:24]};

  // Notes on the sheet:
  //   INVERSE BYTES
endmodule
