// Logisim project Register File Input.circ as structural Verilog: 1 circuit, main circuit main
module main (
  input  [2:0] Selector,
  input  clk,
  input  [31:0] RAM,
  input  [31:0] ALU_Output,
  input  [6:0] Keyboard,
  input  [31:0] High,
  input  KBD_AVAIL,
  input  [31:0] Low,
  output [31:0] RF_Input
);

  wire lw, pop, ram_t;
  wire [31:0] KBD_in, random;

  Random #(.width(32)) Rnd (.clk(clk), .out(random));  // open: next, clr
  or or_1 (ram_t, pop, lw);
  Multiplexer #(.width(32), .enable("false")) multiplexer_1 (
    .in0({32{1'b1}}), .in1({{25{1'b0}}, Keyboard}), .out(KBD_in), .sel(KBD_AVAIL));
  Multiplexer #(.select(3), .width(32), .enable("false")) multiplexer_2 (
    .in0(ALU_Output), .in1(KBD_in), .in2(random), .in3(RAM), .in4(High), .in5(Low), .out(RF_Input),
    .sel(Selector));  // open: in6, in7

  // Other names for the same wires on the sheet: ALU[31:0] = ALU_Output; KBD[6:0] = Keyboard

  // Notes on the sheet:
  //   Register File Input
endmodule
