// Logisim project Switcher.circ as structural Verilog: 1 circuit, main circuit main
module main (
  input  [31:0] Instruction,
  output [3:0] ALU_Op__Sel,
  output [1:0] MA_selector,
  output [2:0] RF_Input_Sel
);

  wire _00_0000, _11_1000, _11_1111, add, addi, \and , andi, beq, bgtz, blez, bltz, bne, comparator_5_eq,
       comparator_6_eq, comparator_7_eq, comparator_8_eq, comparator_13_eq, comparator_14_eq,
       comparator_15_eq, comparator_16_eq, comparator_21_eq, comparator_22_eq, comparator_23_eq,
       comparator_24_eq, comparator_29_eq, comparator_30_eq, comparator_31_eq, comparator_32_eq,
       comparator_33_eq, comparator_34_eq, comparator_36_eq, comparator_37_eq, comparator_38_eq,
       comparator_39_eq, div, divu, halt, j, jr, kbd, lw, mfhi, mflo, mult, mulu, nop, \nor , \or , ori, pop,
       priority_encoder_1_gs, priority_encoder_2_gs, push, ram, rnd, slt, slti, sltiu, sltu, sub, sw, tty,
       \xor , xori;
  wire [1:0] BC_Selector;
  wire [2:0] BC_Flag_Condition, priority_encoder_1_out;
  wire [3:0] priority_encoder_2_out;

  or or_1 (ram, pop, lw);
  Comparator #(.width(6)) comparator_1 (.a(Instruction[31:26]), .b({6{1'b0}}), .eq(_00_0000));  // open: gt, lt
  Comparator #(.width(6)) comparator_2 (.a(Instruction[31:26]), .b(6'b001000), .eq(addi));  // open: gt, lt
  Comparator #(.width(6)) comparator_3 (.a(Instruction[31:26]), .b(6'b001010), .eq(slti));  // open: gt, lt
  Comparator #(.width(6)) comparator_4 (.a(Instruction[31:26]), .b(6'b000110), .eq(blez));  // open: gt, lt
  Comparator #(.width(6)) comparator_5 (.a(Instruction[5:0]), .b(6'b100000), .eq(comparator_5_eq));  // open: gt, lt
  Comparator #(.width(6)) comparator_6 (.a(Instruction[5:0]), .b(6'b011010), .eq(comparator_6_eq));  // open: gt, lt
  Comparator #(.width(6)) comparator_7 (.a(Instruction[5:0]), .b(6'b100111), .eq(comparator_7_eq));  // open: gt, lt
  Comparator #(.width(6)) comparator_8 (.a(Instruction[5:0]), .b(6'b010000), .eq(comparator_8_eq));  // open: gt, lt
  Priority_Encoder #(.disabled(0)) priority_encoder_1 (
    .in1(kbd), .in2(rnd), .in3(ram), .in4(mfhi), .in5(mflo), .out(priority_encoder_1_out), .en_in(1'b1),
    .gs(priority_encoder_1_gs));  // open: in0, in6, in7, en_out
  and and_1 (add, _00_0000, comparator_5_eq);
  and and_2 (div, _00_0000, comparator_6_eq);
  and and_3 (\nor , _00_0000, comparator_7_eq);
  and and_4 (mfhi, _00_0000, comparator_8_eq);
  Multiplexer #(.width(3), .enable("false")) multiplexer_1 (
    .in0(3'b000), .in1(priority_encoder_1_out), .out(RF_Input_Sel), .sel(priority_encoder_1_gs));
  Comparator #(.width(6)) comparator_9 (.a(Instruction[31:26]), .b(6'b111000), .eq(_11_1000));  // open: gt, lt
  Comparator #(.width(6)) comparator_10 (.a(Instruction[31:26]), .b(6'b001100), .eq(andi));  // open: gt, lt
  Comparator #(.width(6)) comparator_11 (.a(Instruction[31:26]), .b(6'b001011), .eq(sltiu));  // open: gt, lt
  Comparator #(.width(6)) comparator_12 (.a(Instruction[31:26]), .b(6'b000111), .eq(bgtz));  // open: gt, lt
  Comparator #(.width(6)) comparator_13 (.a(Instruction[5:0]), .b(6'b100010), .eq(comparator_13_eq));  // open: gt, lt
  Comparator #(.width(6)) comparator_14 (.a(Instruction[5:0]), .b(6'b011011), .eq(comparator_14_eq));  // open: gt, lt
  Comparator #(.width(6)) comparator_15 (.a(Instruction[5:0]), .b(6'b101000), .eq(comparator_15_eq));  // open: gt, lt
  Comparator #(.width(6)) comparator_16 (.a(Instruction[5:0]), .b(6'b010010), .eq(comparator_16_eq));  // open: gt, lt
  and and_5 (sub, _00_0000, comparator_13_eq);
  and and_6 (divu, _00_0000, comparator_14_eq);
  and and_7 (\xor , _00_0000, comparator_15_eq);
  and and_8 (mflo, _00_0000, comparator_16_eq);
  Comparator #(.width(6)) comparator_17 (.a(Instruction[31:26]), .b({6{1'b1}}), .eq(_11_1111));  // open: gt, lt
  Comparator #(.width(6)) comparator_18 (.a(Instruction[31:26]), .b(6'b001101), .eq(ori));  // open: gt, lt
  Comparator #(.width(6)) comparator_19 (.a(Instruction[31:26]), .b(6'b000100), .eq(beq));  // open: gt, lt
  Comparator #(.width(6)) comparator_20 (.a(Instruction[31:26]), .b(6'b000001), .eq(bltz));  // open: gt, lt
  Comparator #(.width(6)) comparator_21 (.a(Instruction[5:0]), .b(6'b011000), .eq(comparator_21_eq));  // open: gt, lt
  Comparator #(.width(6)) comparator_22 (.a(Instruction[5:0]), .b(6'b100100), .eq(comparator_22_eq));  // open: gt, lt
  Comparator #(.width(6)) comparator_23 (.a(Instruction[5:0]), .b(6'b101010), .eq(comparator_23_eq));  // open: gt, lt
  Comparator #(.width(6)) comparator_24 (.a(Instruction[5:0]), .b({6{1'b0}}), .eq(comparator_24_eq));  // open: gt, lt
  or or_2 (MA_selector[1], pop, push);
  or or_3 (MA_selector[0], sw, lw);
  Comparator #(.width(6)) comparator_25 (.a(Instruction[31:26]), .b(6'b000010), .eq(j));  // open: gt, lt
  Comparator #(.width(6)) comparator_26 (.a(Instruction[31:26]), .b(6'b001110), .eq(xori));  // open: gt, lt
  Comparator #(.width(6)) comparator_27 (.a(Instruction[31:26]), .b(6'b000101), .eq(bne));  // open: gt, lt
  Comparator #(.width(6)) comparator_28 (.a(Instruction[31:26]), .b(6'b100011), .eq(lw));  // open: gt, lt
  and and_9 (mult, _00_0000, comparator_21_eq);
  and and_10 (\and , _00_0000, comparator_22_eq);
  and and_11 (slt, _00_0000, comparator_23_eq);
  and and_12 (nop, _00_0000, comparator_24_eq);
  Comparator #(.width(6)) comparator_29 (.a(Instruction[5:0]), .b(6'b011001), .eq(comparator_29_eq));  // open: gt, lt
  Comparator #(.width(6)) comparator_30 (.a(Instruction[5:0]), .b(6'b100101), .eq(comparator_30_eq));  // open: gt, lt
  Comparator #(.width(6)) comparator_31 (.a(Instruction[5:0]), .b(6'b101011), .eq(comparator_31_eq));  // open: gt, lt
  Comparator #(.width(6)) comparator_32 (.a(Instruction[5:0]), .b(6'b001000), .eq(comparator_32_eq));  // open: gt, lt
  Comparator #(.width(6)) comparator_33 (.a(Instruction[5:0]), .b({6{1'b0}}), .eq(comparator_33_eq));  // open: gt, lt
  Comparator #(.width(6)) comparator_34 (.a(Instruction[5:0]), .b(6'b000001), .eq(comparator_34_eq));  // open: gt, lt
  Comparator #(.width(6)) comparator_35 (.a(Instruction[31:26]), .b(6'b101011), .eq(sw));  // open: gt, lt
  and and_13 (mulu, _00_0000, comparator_29_eq);
  and and_14 (\or , _00_0000, comparator_30_eq);
  and and_15 (sltu, _00_0000, comparator_31_eq);
  and and_16 (jr, _00_0000, comparator_32_eq);
  and and_17 (pop, comparator_33_eq, _11_1000);
  and and_18 (push, _11_1000, comparator_34_eq);
  Priority_Encoder #(.select(4), .disabled(0)) priority_encoder_2 (
    .in0(add), .in1(sub), .in2(slt), .in3(sltu), .in4(\and ), .in5(\or ), .in6(\nor ), .in7(\xor ),
    .in8(mult), .in9(mulu), .in10(div), .in11(divu), .out(priority_encoder_2_out), .gs(priority_encoder_2_gs));  // open: in12, in13, in14, in15, en_out, en_in
  Comparator #(.width(6)) comparator_36 (.a(Instruction[5:0]), .b({6{1'b1}}), .eq(comparator_36_eq));  // open: gt, lt
  Comparator #(.width(6)) comparator_37 (.a(Instruction[5:0]), .b(6'b000001), .eq(comparator_37_eq));  // open: gt, lt
  Comparator #(.width(6)) comparator_38 (.a(Instruction[5:0]), .b(6'b000010), .eq(comparator_38_eq));  // open: gt, lt
  Comparator #(.width(6)) comparator_39 (.a(Instruction[5:0]), .b(6'b000100), .eq(comparator_39_eq));  // open: gt, lt
  Multiplexer #(.width(4), .enable("false")) multiplexer_2 (
    .in0(4'b0000), .in1(priority_encoder_2_out), .out(ALU_Op__Sel), .sel(priority_encoder_2_gs));
  and and_19 (halt, _11_1111, comparator_36_eq);
  and and_20 (tty, _11_1111, comparator_37_eq);
  and and_21 (rnd, _11_1111, comparator_38_eq);
  and and_22 (kbd, _11_1111, comparator_39_eq);
  Branch_Control_Selector branch_control_selector_1 (
    .beq(beq), .bne(bne), .blez(blez), .bgtz(bgtz), .bltz(bltz), .jr(jr), .j(j), .BC_Selector(BC_Selector),
    .Flag_Condition(BC_Flag_Condition));

  // Other names for the same wires on the sheet: const[15:0] = Instruction[15:0]; dest[25:0] = Instruction[25:0];
  //   func__code[5:0] = Instruction[5:0]; RD[4:0] = Instruction[15:11]; Rt[4:0] = Instruction[20:16];
  //   Rs[4:0] = Instruction[25:21]; op__code[5:0] = Instruction[31:26]

  // Notes on the sheet:
  //   SWITCHER
  //   RF input selector
  //   MEMORY ADRESS
  //   input selector
  //   ALU OP  SELECTOR
endmodule
